# Fritzing sketch aqo_circuit (saved by Fritzing 0.9.3b)

parts:
  Part1 = Adafruit Feather M0 Express [part_number="Adafruit #3403"]
  Part2 = NeoPixel Stick [part_number=1426]
  Part4 = Lithium Ion Polymer Battery 3.7v 1200mAh [part_number=258]  # not connected
  Part3 = Adafruit SGP30 Gas Sensor

nets:
  GND: Part1.GND, Part2.GND, Part3.GND
  +3V3: Part1.+3V3, Part3.VIN
  N1: Part1.VBUS, Part2.+5V
  N2: Part1.D11, Part2.DATAIN
  N3: Part1.SCL, Part3.SCL
  N4: Part1.SDA, Part3.SDA

custom parts:
  Adafruit Feather M0 Express: We love all our Feathers equally, but this Feather is very special. It's our first Feather that is specifically designed for use with CircuitPython! CircuitPython is our beginner-oriented flavor of MicroPython - and as the name hints at, its a small but full-featured version of the popular Python programming language specifically for use with circuitry and electronics. That doesn't mean you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
  NeoPixel Stick: Make your own little LED strip arrangement with this stick of NeoPixel LEDs. We crammed 8 of the tiny 5050 (5mm x 5mm) smart RGB LEDs onto a PCB with mounting holes and a chainable design. Use only one microcontroller pin to control as many as you can chain together! Each LED is addressable as the driver chip is inside the LED. Each one has ~18mA constant current drive so the color will be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
  Lithium Ion Polymer Battery 3.7v 1200mAh: Lithium ion polymer (also known as 'lipo' or 'lipoly') batteries are thin, light and powerful. The output ranges from 4.2V when completely charged to 3.7V. This battery has a capacity of 1200mAh for a total of about 4.5 Wh. The batteries come pre-attached with a genuine 2-pin JST-PH connector as shown and include the necessary protection circuitry.
